// Logisim project Single Cycle Processor.circ as structural Verilog: 5 circuits, main circuit main
module main (
);

  wire alu_8_1_eq, clock_1_out, controlunit_1_mux2, controlunit_1_read, controlunit_1_we, controlunit_1_write;
  wire [0:0] controlunit_1_branch;
  wire [1:0] and_1_out, controlunit_1_mux1, controlunit_1_pcmux;
  wire [2:0] controlunit_1_alufun;
  wire [7:0] alu_8_1_result, datamem_dout, multiplexer_2_out, multiplexer_3_out, register_file_1_out_7,
       register_file_1_out_8;
  wire [9:0] adder_1_out, adder_2_out, multiplexer_1_out, pc_1_out_3;
  wire [20:0] rom_1_data;

  Clock clock_1 (.out(clock_1_out));
  Adder #(.width(10)) adder_1 (.a(pc_1_out_3), .b(10'h1), .out(adder_1_out));  // open: cin, cout
  Multiplexer #(.select(2), .width(10)) multiplexer_1 (
    .in0(adder_1_out), .in1(adder_2_out), .in2({2'b00, rom_1_data[7:0]}), .out(multiplexer_1_out),
    .sel(and_1_out));  // open: in3
  assign and_1_out = controlunit_1_pcmux & {1'b0, controlunit_1_branch[0]};  // AND_Gate and_1, 2 bits wide
  PC pc_1 (.in_1(multiplexer_1_out), .CLK(clock_1_out), .out_3(pc_1_out_3));
  Adder #(.width(10)) adder_2 (.a({2'b00, rom_1_data[7:0]}), .b(pc_1_out_3), .out(adder_2_out));  // open: cin, cout
  ROM #(.addrWidth(10), .dataWidth(21)) rom_1 (.addr(pc_1_out_3), .data(rom_1_data));
  Multiplexer #(.select(2), .width(8)) multiplexer_2 (
    .in0(rom_1_data[7:0]), .in2(alu_8_1_result), .in3(datamem_dout), .out(multiplexer_2_out),
    .sel(controlunit_1_mux1));  // open: in1
  controlunit controlunit_1 (
    .opcode(rom_1_data[20:17]), .EQ(alu_8_1_eq), .ALUfun(controlunit_1_alufun), .Mux1(controlunit_1_mux1),
    .Mux2(controlunit_1_mux2), .WE(controlunit_1_we), .Write(controlunit_1_write), .Read(controlunit_1_read),
    .PCmux(controlunit_1_pcmux), .Branch(controlunit_1_branch[0]));
  Register_file register_file_1 (
    .WE(controlunit_1_we), .RD(rom_1_data[10:8]), .input1(multiplexer_2_out), .CLK(clock_1_out),
    .RS(rom_1_data[16:14]), .RT(rom_1_data[13:11]), .out_7(register_file_1_out_7),
    .out_8(register_file_1_out_8));
  Multiplexer #(.width(8)) multiplexer_3 (
    .in0(register_file_1_out_8), .in1(rom_1_data[7:0]), .out(multiplexer_3_out), .sel(controlunit_1_mux2));
  ALU_8 alu_8_1 (
    .X(register_file_1_out_7), .Y(multiplexer_3_out), .ALUfunc(controlunit_1_alufun),
    .RESULT(alu_8_1_result), .EQ(alu_8_1_eq));
  RAM #(.asyncread("true"), .trigger("falling")) datamem (
    .addr(alu_8_1_result), .we(controlunit_1_write), .oe(controlunit_1_read), .clk(clock_1_out),
    .din(register_file_1_out_8), .dout(datamem_dout));

  // Notes on the sheet:
  //   contents of rom_1 (hex, n*v repeats v):
  //   60306 60601 6040c 1f700 1f3d00 f7004 160009 b200
endmodule

module Register_file (
  input  WE,
  input  [2:0] RD,
  input  [7:0] input1,
  input  CLK,
  input  [2:0] RS,
  input  [2:0] RT,
  output [7:0] out_7,
  output [7:0] out_8
);

  wire decoder_1_out0, decoder_1_out1, decoder_1_out2, decoder_1_out3, decoder_1_out4, decoder_1_out5,
       decoder_1_out6, decoder_1_out7;
  wire [7:0] r0_q, r1_q, r2_q, r3_q, r4_q, r5_q, r6_q, r7_q;

  Decoder #(.select(3)) decoder_1 (
    .out0(decoder_1_out0), .out1(decoder_1_out1), .out2(decoder_1_out2), .out3(decoder_1_out3),
    .out4(decoder_1_out4), .out5(decoder_1_out5), .out6(decoder_1_out6), .out7(decoder_1_out7), .sel(RD),
    .en(WE));
  Multiplexer #(.select(3), .width(8)) multiplexer_1 (
    .in0(r0_q), .in1(r1_q), .in2(r2_q), .in3(r3_q), .in4(r4_q), .in5(r5_q), .in6(r6_q), .in7(r7_q),
    .out(out_7), .sel(RS));
  Multiplexer #(.select(3), .width(8)) multiplexer_2 (
    .in0(r0_q), .in1(r1_q), .in2(r2_q), .in3(r3_q), .in4(r4_q), .in5(r5_q), .in6(r6_q), .in7(r7_q),
    .out(out_8), .sel(RT));
  Register #(.trigger("falling")) r0 (.D(input1), .en(decoder_1_out0), .clk(CLK), .Q(r0_q));  // open: clr
  Register #(.trigger("falling")) r1 (.D(input1), .en(decoder_1_out1), .clk(CLK), .Q(r1_q));  // open: clr
  Register #(.trigger("falling")) r2 (.D(input1), .en(decoder_1_out2), .clk(CLK), .Q(r2_q));  // open: clr
  Register #(.trigger("falling")) r3 (.D(input1), .en(decoder_1_out3), .clk(CLK), .Q(r3_q));  // open: clr
  Register #(.trigger("falling")) r4 (.D(input1), .en(decoder_1_out4), .clk(CLK), .Q(r4_q));  // open: clr
  Register #(.trigger("falling")) r5 (.D(input1), .en(decoder_1_out5), .clk(CLK), .Q(r5_q));  // open: clr
  Register #(.trigger("falling")) r6 (.D(input1), .en(decoder_1_out6), .clk(CLK), .Q(r6_q));  // open: clr
  Register #(.trigger("falling")) r7 (.D(input1), .en(decoder_1_out7), .clk(CLK), .Q(r7_q));  // open: clr
endmodule

module PC (
  input  [9:0] in_1,
  input  CLK,
  output [9:0] out_3
);

  Register #(.width(10)) register_1 (.D(in_1), .en(CLK), .clk(CLK), .Q(out_3));  // open: clr
endmodule

module ALU_8 (
  input  [7:0] X,
  input  [7:0] Y,
  input  [2:0] ALUfunc,
  output [7:0] RESULT,
  output EQ
);

  wire comparator_1_lt;
  wire [7:0] adder_1_out, and_1_out, bit_extender_1_out, or_1_out, shifter_1_out;

  Comparator comparator_1 (.a(Y), .b(X), .eq(EQ), .lt(comparator_1_lt));  // open: gt
  Adder adder_1 (.a(X), .b(Y), .out(adder_1_out));  // open: cin, cout
  Shifter #(.shift("rl")) shifter_1 (.in(X), .\dist (Y[2:0]), .out(shifter_1_out));
  assign and_1_out = X & Y;  // AND_Gate and_1, 8 bits wide
  assign or_1_out = X | Y;  // OR_Gate or_1, 8 bits wide
  assign bit_extender_1_out = {{7{comparator_1_lt}}, comparator_1_lt};  // Bit_Extender bit_extender_1
  Multiplexer #(.select(3), .width(8)) multiplexer_1 (
    .in0(adder_1_out), .in1(and_1_out), .in2(or_1_out), .in3(shifter_1_out), .in4(bit_extender_1_out),
    .out(RESULT), .sel(ALUfunc));  // open: in5, in6, in7
endmodule

module controlunit (
  input  [3:0] opcode,
  input  EQ,
  output [2:0] ALUfun,
  output [1:0] Mux1,
  output Mux2,
  output WE,
  output Write,
  output Read,
  output [1:0] PCmux,
  output Branch
);

  wire and_4_out, and_5_out, and_7_out, and_8_out, and_9_out, and_10_out, and_11_out, and_16_out, and_17_out,
       and_18_out, not_1_out, not_2_out, not_3_out, not_4_out, not_5_out;

  not not_1 (not_1_out, opcode[3]);
  not not_2 (not_2_out, opcode[2]);
  not not_3 (not_3_out, opcode[1]);
  not not_4 (not_4_out, opcode[0]);
  not not_5 (not_5_out, EQ);
  and and_1 (ALUfun[2], opcode[3], opcode[0]);
  and and_2 (ALUfun[1], opcode[3], not_3_out);
  and and_3 (ALUfun[0], opcode[2], not_3_out);
  and and_4 (and_4_out, not_1_out, not_2_out, not_4_out);
  and and_5 (and_5_out, not_2_out, opcode[1]);
  and and_6 (Mux1[0], not_3_out, opcode[0]);
  and and_7 (and_7_out, not_2_out, opcode[0]);
  and and_8 (and_8_out, not_2_out, opcode[1]);
  and and_9 (and_9_out, not_1_out, not_2_out, opcode[0]);
  and and_10 (and_10_out, opcode[3], opcode[2]);
  and and_11 (and_11_out, not_3_out, not_4_out);
  and and_12 (Write, opcode[1], not_4_out);
  and and_13 (Read, not_2_out, not_3_out, opcode[0]);
  and and_14 (PCmux[1], opcode[3], not_2_out, opcode[0]);
  and and_15 (PCmux[0], not_1_out, opcode[2], opcode[0]);
  and and_16 (and_16_out, not_1_out, opcode[2], not_3_out, opcode[0], EQ);
  and and_17 (and_17_out, not_1_out, opcode[2], opcode[1], not_5_out);
  and and_18 (and_18_out, opcode[3], not_2_out, opcode[0]);
  or or_1 (Mux1[1], and_4_out, and_5_out);
  or or_2 (Mux2, and_7_out, and_8_out);
  or or_3 (WE, and_9_out, and_10_out, and_11_out);
  or or_4 (Branch, and_16_out, and_17_out, and_18_out);
endmodule
